// Digital circuit ALU.dig as structural Verilog
module ALU (
  input  [31:0] arg1,
  input  [31:0] f3,
  input  [31:0] f7,
  input  [31:0] arg2,
  output out
);

  wire multiplexer_1_out, multiplexer_2_out, sll, sra, srl;
  wire [0:0] slt, sltu;
  wire [31:0] add, \and , \or , sub, \xor ;

  assign \xor  = arg1 ^ arg2;  // XOr xor_1, 32 bits wide
  assign \or  = arg1 | arg2;  // Or or_1, 32 bits wide
  assign \and  = arg1 | arg2;  // Or or_2, 32 bits wide
  Add #(.Bits(32)) add_1 (.a(arg1), .b(arg2), .c_i(1'b0), .s(add));  // open: c_o
  Sub #(.Bits(32)) sub_1 (.a(arg1), .b(arg2), .c_i(1'b0), .s(sub));  // open: c_o
  BarrelShifter u_sll (.in(arg1[0]), .shift({1'b0, arg2[4:0]}), .out(sll));
  BarrelShifter u_srl (.in(arg1[0]), .shift({1'b0, arg2[4:0]}), .out(srl));
  BarrelShifter u_sra (.in(arg1[0]), .shift({2'b00, arg2[4:0]}), .out(sra));
  Comparator u_slt (.a(arg1[0]), .b(arg2[0]), .lt(slt[0]));  // open: gt, eq
  Comparator u_sltu (.a(arg1[0]), .b(arg2[0]), .lt(sltu[0]));  // open: gt, eq
  Multiplexer multiplexer_1 (.sel(f7[0]), .in_0(add[0]), .in_1(sub[0]), .out(multiplexer_1_out));
  Multiplexer multiplexer_2 (.sel(f7[0]), .in_0(sra), .in_1(srl), .out(multiplexer_2_out));
  Multiplexer #(.Selector_Bits(3)) multiplexer_3 (
    .sel(f3[2:0]), .in_0(multiplexer_1_out), .in_1(sll), .in_2(slt[0]), .in_3(sltu[0]), .in_4(\xor [0]),
    .in_5(multiplexer_2_out), .in_6(\or [0]), .in_7(\and [0]), .out(out));
  // Probe bin on out
  // Probe dec on out
  // Probe hex on out
  // Pins of 1 and 32 bits meet at arg1
  // Pins of 3 and 32 bits meet at f3
  // Pins of 1 and 32 bits meet at f7
  // Pins of 1 and 32 bits meet at arg2
  // Pins of 1 and 32 bits meet at add
  // Pins of 1 and 32 bits meet at sub
  // Pins of 1 and 32 bits meet at \xor 
  // Pins of 1 and 32 bits meet at \or 
  // Pins of 1 and 32 bits meet at \and 
  // Pins of 1 and 32 bits meet at {32{1'b0}}
  // Pins of 1 and 32 bits meet at {32{1'b0}}
  // Pins of 31 and 32 bits meet at {32{1'b0}}
endmodule
