// Digital circuit RISCV.dig as structural Verilog
module RISCV (
  input  reset
);

  wire brinst, clock, control_1_p2, deq, dge, dgeu, dlt, dltu, dmwen, func3, func7, inst, jal_jalr, load,
       notconnected_1_out, notconnected_2_out, notconnected_3_out, opcode, pc_jump, rfwren, rs1, rs1_pc, rs2,
       srai_sub, store;
  wire [1:0] wbsel;
  wire [4:0] datamemory_1_p7, notconnected_4_out, rd;
  wire [31:0] add_1_s, alu, imm, multiplexer_1_out, multiplexer_2_out, multiplexer_3_out, pc, rd1, rd2;

  Multiplexer #(.Bits(32)) multiplexer_1 (.sel(pc_jump), .in_0(add_1_s), .in_1(alu), .out(multiplexer_1_out));
  // NotConnected on notconnected_1_out
  // ProgramCounter programcounter_1: pin names not known; wires that end beside it: multiplexer_1_out, notconnected_1_out, 32'h1, reset, clock, pc
  // ProgramMemory programmemory_1: pin names not known; wires that end beside it: pc, inst
  Add #(.Bits(32)) add_1 (.a(pc), .b(32'h4), .c_i(1'b0), .s(add_1_s));  // open: c_o
  // instdecoder instdecoder_1: pin names not known; wires that end beside it: inst, rd, rs1, rs2
  // unitimm unitimm_1: pin names not known; wires that end beside it: inst, imm
  // Control control_1: pin names not known; wires that end beside it: inst, control_1_p2, rfwren, func3, srai_sub, func7, opcode, wbsel, dmwen, jal_jalr, store, brinst, load
  // registerfile registerfile_1: pin names not known; wires that end beside it: rfwren, rd, rd, rs1, rs2, clock, rd1, rd2
  Multiplexer #(.Bits(32)) multiplexer_2 (.sel(control_1_p2), .in_0(rd2), .in_1(imm), .out(multiplexer_2_out));
  Multiplexer #(.Bits(32)) multiplexer_3 (.sel(rs1_pc), .in_0(rd1), .in_1(pc), .out(multiplexer_3_out));
  // Branch branch_1: pin names not known; wires that end beside it: rd1, rd2, brinst, func3, jal_jalr, rs1_pc, pc_jump, deq, dlt, dge, dltu, dgeu
  // alu__1 alu__1_1: pin names not known; wires that end beside it: func3, multiplexer_3_out, srai_sub, multiplexer_2_out, alu
  // NotConnected on notconnected_2_out
  // NotConnected on notconnected_3_out
  // DataMemory datamemory_1: pin names not known; wires that end beside it: dmwen, alu, notconnected_2_out, notconnected_3_out, rd2, clock, datamemory_1_p7
  Button button_1 (.out(clock));
  Multiplexer #(.Selector_Bits(2), .Bits(5)) multiplexer_4 (
    .sel(wbsel), .in_0(alu[4:0]), .in_1(datamemory_1_p7), .in_2(add_1_s[4:0]), .in_3(notconnected_4_out),
    .out(rd));
  // NotConnected on notconnected_4_out[0]
  // Pins of 5 and 32 bits meet at add_1_s
  // Pins of 5 and 32 bits meet at alu
  // Pins of 1 and 5 bits meet at notconnected_4_out
endmodule
